// Logisim project cpu.circ as structural Verilog: 1 circuit, main circuit cpu
module cpu (
  input  clk,
  input  [31:0] INSTRUCTION,
  input  [31:0] MEM_READ_DATA,
  output [31:0] MEM_WRITE_ADDRESS,
  output [31:0] PROGRAM_COUNTER,
  output [31:0] ra,
  output [31:0] sp,
  output [31:0] t0,
  output [31:0] t1,
  output [31:0] t2,
  output [31:0] s0,
  output [31:0] s1,
  output [31:0] a0,
  output [31:0] tohost,
  output [3:0] MEM_WRITE_ENABLE,
  output [31:0] MEM_WRITE_DATA
);

  wire As, Be, Blt, Bs, Bu, comparator_1_eq, comparator_2_eq, comparator_3_eq, comparator_4_eq,
       comparator_5_eq, comparator_6_eq, comparator_7_eq, CSs, CSw, Mrw, not_1_out, PCSel, RWEn;
  wire [1:0] bit_extender_1_out, load, store_whb, Ws;
  wire [2:0] ISel;
  wire [3:0] ALs, multiplexer_9_out, multiplexer_10_out;
  wire [9:0] and_7_out;
  wire [31:0] and_2_out, and_3_out, and_4_out, and_5_out, and_6_out, imm1, MEM_READ_DATA1, MEM_READ_DATA_LB,
       MEM_READ_DATA_LH, MEM_WRITE_DATA_SB, MEM_WRITE_DATA_SH, multiplexer_2_out, multiplexer_3_out,
       multiplexer_4_out, PC4, PC_NEW, read_data1, read_data2, result1, shifter_1_out, shifter_2_out,
       shifter_3_out, shifter_4_out, shifter_5_out, shifter_6_out, shifter_7_out, shifter_8_out,
       shifter_9_out, shifter_10_out, shifter_11_out, writeback;

  Adder #(.width(32)) adder_1 (.a(PROGRAM_COUNTER), .b(32'h4), .out(PC4));  // open: cin, cout
  Register #(.width(32)) PC (.D(PC_NEW), .clk(clk), .Q(PROGRAM_COUNTER));  // open: en, clr
  Multiplexer #(.enable("false"), .width(32)) multiplexer_1 (.in0(PC4), .in1(result1), .out(PC_NEW), .sel(PCSel));
  control_logic control_logic_1 (
    .CSRWen(CSw), .PCSel(PCSel), .RegWEn(RWEn), .ImmSel(ISel), .BrUn(Bu), .ASel(As), .BSel(Bs), .ALUSel(ALs),
    .MemRW(Mrw), .WBSel(Ws), .CSRSel(CSs), .inst(INSTRUCTION), .BrEq(Be), .BrLt(Blt));
  Multiplexer #(.enable("false"), .width(32)) multiplexer_2 (
    .in0(result1), .in1(imm1), .out(multiplexer_2_out), .sel(CSs));
  regfile regfile_1 (
    .rs1(INSTRUCTION[19:15]), .rs2(INSTRUCTION[24:20]), .rd(INSTRUCTION[11:7]), .Write_Data(writeback),
    .RegWEn(RWEn), .clk(clk), .ra(ra), .sp(sp), .t0(t0), .t1(t1), .t2(t2), .s0(s0), .s1(s1), .a0(a0),
    .Read_Data_1(read_data1), .Read_Data_2(read_data2));
  imm_gen imm_gen_1 (.inst(INSTRUCTION), .ImmSel(ISel), .imm(imm1));
  csr csr_1 (.CSR_address(12'h51e), .CSR_din(multiplexer_2_out), .CSR_WE(CSw), .clk(clk), .tohost(tohost));
  Multiplexer #(.enable("false"), .width(32)) multiplexer_3 (
    .in0(read_data1), .in1(PROGRAM_COUNTER), .out(multiplexer_3_out), .sel(As));
  Multiplexer #(.enable("false"), .width(32)) multiplexer_4 (
    .in0(read_data2), .in1(imm1), .out(multiplexer_4_out), .sel(Bs));
  alu alu_1 (.Result(result1), .A(multiplexer_3_out), .B(multiplexer_4_out), .ALUSel(ALs));
  branch_comp branch_comp_1 (.rs1(read_data1), .rs2(read_data2), .BrUn(Bu), .BrEq(Be), .BrLt(Blt));
  Bit_Extender #(.in_width(32), .out_width(2), .\type ("zero")) bit_extender_1 (.in(result1), .out(bit_extender_1_out));
  assign MEM_WRITE_ADDRESS = result1 & 32'hfffffffc;  // AND_Gate and_1, 32 bits wide
  Shifter #(.width(32)) shifter_1 (.in(MEM_READ_DATA), .\dist (5'b10000), .out(shifter_1_out));
  Shifter #(.shift("ar"), .width(32)) shifter_2 (.in(MEM_READ_DATA), .\dist (5'b10000), .out(shifter_2_out));
  Shifter #(.width(32)) shifter_3 (.in(MEM_READ_DATA), .\dist (5'b11000), .out(shifter_3_out));
  Shifter #(.shift("ar"), .width(32)) shifter_4 (.in(shifter_3_out), .\dist (5'b11000), .out(shifter_4_out));
  Shifter #(.width(32)) shifter_5 (.in(MEM_READ_DATA), .\dist (5'b10000), .out(shifter_5_out));
  Shifter #(.shift("ar"), .width(32)) shifter_6 (.in(shifter_5_out), .\dist (5'b11000), .out(shifter_6_out));
  Shifter #(.width(32)) shifter_7 (.in(MEM_READ_DATA), .\dist (5'b01000), .out(shifter_7_out));
  Shifter #(.shift("ar"), .width(32)) shifter_8 (.in(shifter_7_out), .\dist (5'b11000), .out(shifter_8_out));
  Shifter #(.shift("ar"), .width(32)) shifter_9 (.in(MEM_READ_DATA), .\dist (5'b11000), .out(shifter_9_out));
  Multiplexer #(.enable("false"), .select(2), .width(32)) multiplexer_5 (
    .in0(MEM_READ_DATA_LB), .in1(MEM_READ_DATA_LH), .in2(MEM_READ_DATA), .out(MEM_READ_DATA1), .sel(load));  // open: in3
  Multiplexer #(.enable("false"), .select(2), .width(32)) multiplexer_6 (
    .in1(result1), .in2(MEM_READ_DATA1), .in3(PC4), .out(writeback), .sel(Ws));  // open: in0
  Comparator #(.width(10)) comparator_1 (
    .a({INSTRUCTION[14:12], INSTRUCTION[6:0]}), .b(10'h3), .eq(comparator_1_eq));  // open: gt, lt
  Comparator #(.width(10)) comparator_2 (
    .a({INSTRUCTION[14:12], INSTRUCTION[6:0]}), .b(10'h83), .eq(comparator_2_eq));  // open: gt, lt
  Comparator #(.width(10)) comparator_3 (
    .a({INSTRUCTION[14:12], INSTRUCTION[6:0]}), .b(10'h103), .eq(comparator_3_eq));  // open: gt, lt
  Shifter #(.shift("ar"), .width(32)) shifter_10 (.in(shifter_1_out), .\dist (5'b10000), .out(shifter_10_out));
  Multiplexer #(.enable("false"), .width(32)) multiplexer_7 (
    .in0(shifter_10_out), .in1(shifter_2_out), .out(MEM_READ_DATA_LH), .sel(result1[1]));
  Priority_Encoder #(.select(2)) priority_encoder_1 (
    .in0(comparator_1_eq), .in1(comparator_2_eq), .in2(comparator_3_eq), .out(load));  // open: in3, gs, en_out, en_in
  Multiplexer #(.enable("false"), .select(2), .width(32)) multiplexer_8 (
    .in0(shifter_4_out), .in1(shifter_6_out), .in2(shifter_8_out), .in3(shifter_9_out),
    .out(MEM_READ_DATA_LB), .sel(bit_extender_1_out));
  assign and_2_out = read_data2 & 32'hffff;  // AND_Gate and_2, 32 bits wide
  assign and_3_out = read_data2 & 32'hff;  // AND_Gate and_3, 32 bits wide
  assign and_4_out = read_data2 & 32'hff00;  // AND_Gate and_4, 32 bits wide
  assign and_5_out = read_data2 & 32'hff0000;  // AND_Gate and_5, 32 bits wide
  assign and_6_out = read_data2 & 32'hff000000;  // AND_Gate and_6, 32 bits wide
  Multiplexer #(.enable("false"), .select(2), .width(4)) multiplexer_9 (
    .in0(4'b0001), .in1(4'b0010), .in2(4'b0100), .in3(4'b1000), .out(multiplexer_9_out), .sel(result1[1:0]));
  Multiplexer #(.enable("false"), .width(4)) multiplexer_10 (
    .in0(4'b0011), .in1(4'b1100), .out(multiplexer_10_out), .sel(result1[1]));
  Multiplexer #(.enable("false"), .width(32)) multiplexer_11 (
    .in0(and_2_out), .in1(shifter_11_out), .out(MEM_WRITE_DATA_SH), .sel(result1[1]));
  Shifter #(.width(32)) shifter_11 (.in(read_data2), .\dist (5'b10000), .out(shifter_11_out));
  assign and_7_out = {INSTRUCTION[14:12], INSTRUCTION[6:0]} & 10'h7f;  // AND_Gate and_7, 10 bits wide
  Multiplexer #(.enable("false"), .select(2), .width(32)) multiplexer_12 (
    .in0(MEM_WRITE_DATA_SB), .in1(MEM_WRITE_DATA_SH), .in2(read_data2), .in3(read_data2),
    .out(MEM_WRITE_DATA), .sel(store_whb));
  Multiplexer #(.enable("false"), .select(2), .width(32)) multiplexer_13 (
    .in0(and_3_out), .in1(and_4_out), .in2(and_5_out), .in3(and_6_out), .out(MEM_WRITE_DATA_SB),
    .sel(result1[1:0]));
  Comparator #(.width(10)) comparator_4 (
    .a({INSTRUCTION[14:12], INSTRUCTION[6:0]}), .b(10'h23), .eq(comparator_4_eq));  // open: gt, lt
  Comparator #(.width(10)) comparator_5 (
    .a({INSTRUCTION[14:12], INSTRUCTION[6:0]}), .b(10'ha3), .eq(comparator_5_eq));  // open: gt, lt
  Comparator #(.width(10)) comparator_6 (
    .a({INSTRUCTION[14:12], INSTRUCTION[6:0]}), .b(10'h123), .eq(comparator_6_eq));  // open: gt, lt
  not not_1 (not_1_out, comparator_7_eq);
  Comparator #(.width(10)) comparator_7 (.a(and_7_out), .b(10'h23), .eq(comparator_7_eq));  // open: gt, lt
  Multiplexer #(.enable("false"), .select(2), .width(4)) multiplexer_14 (
    .in0(multiplexer_9_out), .in1(multiplexer_10_out), .in2(4'b1111), .in3(4'b0000), .out(MEM_WRITE_ENABLE),
    .sel(store_whb));
  Priority_Encoder #(.select(2)) priority_encoder_2 (
    .in0(comparator_4_eq), .in1(comparator_5_eq), .in2(comparator_6_eq), .in3(not_1_out), .out(store_whb));  // open: gs, en_out, en_in

  // Notes on the sheet:
  //   Output to IMEM
  //   IMEM (do **NOT** move this)
  //   Inputs from IMEM
  //   It is OK to move the PC, RegFile, ALU, MEM, Branch Comp, Imm Gen, and Control Logic to wherever is most convenient for you when constructing your CPU, and to delete this text
  //   Inputs/Outputs for testing. Do **NOT** move these.
  //   Outputs To DMEM
  //   DMEM (do **NOT** move this)
  //   Inputs From DMEM
endmodule
