// Logisim project regfile.circ as structural Verilog: 1 circuit, main circuit regfile
module regfile (
  input  [4:0] rs1,
  input  [4:0] rs2,
  input  [4:0] rd,
  input  [31:0] Write_Data,
  input  RegWEn,
  input  clk,
  output [31:0] ra,
  output [31:0] sp,
  output [31:0] t0,
  output [31:0] t1,
  output [31:0] t2,
  output [31:0] s0,
  output [31:0] s1,
  output [31:0] a0,
  output [31:0] Read_Data_1,
  output [31:0] Read_Data_2
);

  wire and_1_out, and_2_out, and_3_out, and_4_out, and_5_out, and_6_out, and_7_out, and_8_out, and_9_out,
       and_10_out, and_11_out, comparator_1_eq, comparator_2_eq, comparator_3_eq, comparator_4_eq,
       comparator_5_eq, comparator_6_eq, comparator_7_eq, comparator_8_eq, comparator_9_eq, comparator_10_eq,
       comparator_11_eq;
  wire [31:0] a0i, rai, s0i, s1i, s4, s4i, spi, t0i, t1i, t2i, t6, t6i, tp, tpi, x0, x0i;

  Comparator #(.width(5)) comparator_1 (.a(rd), .b(5'b00001), .eq(comparator_1_eq));  // open: gt, lt
  Comparator #(.width(5)) comparator_2 (.a(rd), .b(5'b00010), .eq(comparator_2_eq));  // open: gt, lt
  Comparator #(.width(5)) comparator_3 (.a(rd), .b(5'b00101), .eq(comparator_3_eq));  // open: gt, lt
  Comparator #(.width(5)) comparator_4 (.a(rd), .b(5'b00110), .eq(comparator_4_eq));  // open: gt, lt
  Comparator #(.width(5)) comparator_5 (.a(rd), .b(5'b00111), .eq(comparator_5_eq));  // open: gt, lt
  Comparator #(.width(5)) comparator_6 (.a(rd), .b(5'b01000), .eq(comparator_6_eq));  // open: gt, lt
  Comparator #(.width(5)) comparator_7 (.a(rd), .b(5'b01001), .eq(comparator_7_eq));  // open: gt, lt
  Comparator #(.width(5)) comparator_8 (.a(rd), .b(5'b01010), .eq(comparator_8_eq));  // open: gt, lt
  Comparator #(.width(5)) comparator_9 (.a(rd), .b(5'b10100), .eq(comparator_9_eq));  // open: gt, lt
  Comparator #(.width(5)) comparator_10 (.a(rd), .b({5{1'b1}}), .eq(comparator_10_eq));  // open: gt, lt
  Comparator #(.width(5)) comparator_11 (.a(rd), .b(5'b00100), .eq(comparator_11_eq));  // open: gt, lt
  Register #(.width(32)) register_1 (.D(rai), .en(and_1_out), .clk(clk), .Q(ra));  // open: clr
  and and_1 (and_1_out, comparator_1_eq, RegWEn);
  Register #(.width(32)) register_2 (.D(spi), .en(and_2_out), .clk(clk), .Q(sp));  // open: clr
  and and_2 (and_2_out, comparator_2_eq, RegWEn);
  Register #(.width(32)) register_3 (.D(t0i), .en(and_3_out), .clk(clk), .Q(t0));  // open: clr
  and and_3 (and_3_out, comparator_3_eq, RegWEn);
  Register #(.width(32)) register_4 (.D(t1i), .en(and_4_out), .clk(clk), .Q(t1));  // open: clr
  and and_4 (and_4_out, comparator_4_eq, RegWEn);
  Register #(.width(32)) register_5 (.D(t2i), .en(and_5_out), .clk(clk), .Q(t2));  // open: clr
  and and_5 (and_5_out, comparator_5_eq, RegWEn);
  Register #(.width(32)) register_6 (.D(s0i), .en(and_6_out), .clk(clk), .Q(s0));  // open: clr
  and and_6 (and_6_out, comparator_6_eq, RegWEn);
  Register #(.width(32)) register_7 (.D(s1i), .en(and_7_out), .clk(clk), .Q(s1));  // open: clr
  and and_7 (and_7_out, comparator_7_eq, RegWEn);
  Register #(.width(32)) register_8 (.D(a0i), .en(and_8_out), .clk(clk), .Q(a0));  // open: clr
  and and_8 (and_8_out, comparator_8_eq, RegWEn);
  Register #(.width(32)) register_9 (.D(s4i), .en(and_9_out), .clk(clk), .Q(s4));  // open: clr
  and and_9 (and_9_out, comparator_9_eq, RegWEn);
  Register #(.width(32)) register_10 (.D(t6i), .en(and_10_out), .clk(clk), .Q(t6));  // open: clr
  and and_10 (and_10_out, comparator_10_eq, RegWEn);
  Register #(.width(32)) register_11 (.D(tpi), .en(and_11_out), .clk(clk), .Q(tp));  // open: clr
  and and_11 (and_11_out, comparator_11_eq, RegWEn);
  Demultiplexer #(.enable("false"), .select(5), .width(32)) demultiplexer_1 (
    .out0(x0i), .out1(rai), .out2(spi), .out4(tpi), .out5(t0i), .out6(t1i), .out7(t2i), .out8(s0i),
    .out9(s1i), .out10(a0i), .out20(s4i), .out31(t6i), .in(Write_Data), .sel(rd));  // open: out3, out11, out12, out13, out14, out15, out16, out17, out18, out19, out21, out22, out23, out24, out25, out26, out27, out28, out29, out30
  Register #(.width(32)) register_12 (.D({32{1'b0}}), .clk(clk), .Q(x0));  // open: en, clr
  Multiplexer #(.enable("false"), .select(5), .width(32)) multiplexer_1 (
    .in0(x0), .in1(ra), .in2(sp), .in4(tp), .in5(t0), .in6(t1), .in7(t2), .in8(s0), .in9(s1), .in10(a0),
    .in20(s4), .in31(t6), .out(Read_Data_1), .sel(rs1));  // open: in3, in11, in12, in13, in14, in15, in16, in17, in18, in19, in21, in22, in23, in24, in25, in26, in27, in28, in29, in30
  Multiplexer #(.enable("false"), .select(5), .width(32)) multiplexer_2 (
    .in0(x0), .in1(ra), .in2(sp), .in4(tp), .in5(t0), .in6(t1), .in7(t2), .in8(s0), .in9(s1), .in10(a0),
    .in20(s4), .in31(t6), .out(Read_Data_2), .sel(rs2));  // open: in3, in11, in12, in13, in14, in15, in16, in17, in18, in19, in21, in22, in23, in24, in25, in26, in27, in28, in29, in30

  // Other names for the same wires on the sheet: read_data1[31:0] = Read_Data_1; read_data2[31:0] = Read_Data_2;
  //   read_reg1[4:0] = rs1; read_reg2[4:0] = rs2; write_en = RegWEn; write_reg[4:0] = rd

  // Notes on the sheet:
  //   INPUTS to your circuit
  //   DON'T CHANGE THE LOCATIONS OF THE INPUTS AND OUTPUTS!
  //   These are DEBUG/TEST outputs from your circuit.
  //   OUTPUTS from your circuit
endmodule
